# Fritzing sketch servo-motor-single-motor (saved by Fritzing 0.9.4)

parts:
  Part1 = Arduino Uno (Rev3)
  J2 = Basic Servo

nets:
  N1: Part1.D10_PWM/SS, J2.pulse
  5V: Part1.5V, J2.vcc
  GND: Part1.GND, J2.gnd
